// Logisim project s-mips.circ as structural Verilog: 22 circuits, main circuit S-MIPS Board
module S_MIPS_Board (
  input  DESHABILITAR_DISPATCHER,
  output halt
);

  wire button_1_out, CLK, CS, d_ff_1_q, LCLR, LoadRAM, LoadRAMOn, LW, R_R_W, R_W, ram_dispatcher_1_finished,
       RCS, Reset_out, RST, TTY_EN;
  wire [2:0] KDB;
  wire [3:0] LMask, Mask, ram_1_read_time, ram_1_write_time, RMask;
  wire [6:0] KDB_DATA, TTY_DATA;
  wire [15:0] Addr, LAddr, RAddr;
  wire [31:0] I0, I1, I2, I3, LData, ram_1_data_out_0, ram_1_data_out_1, ram_1_data_out_2, ram_1_data_out_3,
       RI0, RI1, RI2, RI3;

  TTY #(.rows(25), .cols(80)) tty_1 (.data(TTY_DATA), .clk(CLK), .we(TTY_EN), .clr(RST));
  not not_1 (LoadRAMOn, ram_dispatcher_1_finished);
  RAM_Dispatcher ram_dispatcher_1 (
    .WriteTime(ram_1_write_time), .Clock(CLK), .Data(LData), .Address(LAddr), .Mask(LMask),
    .Finished(ram_dispatcher_1_finished), .Write(LW), .CLR(LCLR));
  Keyboard #(.buflen(64)) keyboard_1 (.clk(CLK), .re(KDB[0]), .avail(KDB[2]), .data(KDB_DATA));  // open: clr
  RAM ram_1 (
    .Address(RAddr), .Data_Out_0(ram_1_data_out_0), .Data_Out_1(ram_1_data_out_1),
    .Data_Out_2(ram_1_data_out_2), .Data_Out_3(ram_1_data_out_3), .Data_In_0(RI0), .Data_In_1(RI1),
    .Data_In_2(RI2), .Data_In_3(RI3), .Mask(RMask), .nRead_Write(R_R_W), .Chip_Select(RCS),
    .Read_Time(ram_1_read_time), .Reset(button_1_out), .Write_Time(ram_1_write_time));
  Button button_1 (.out(button_1_out));
  D_Flip_Flop d_ff_1 (.clk(CLK), .D(1'b1), .Q(d_ff_1_q), .reset(Reset_out));  // open: Qn, preset, en
  Button Reset (.out(Reset_out));
  S_MIPS s_mips_1 (
    .Kbd_Enable(KDB[0]), .Address(Addr), .Kbd_Clear(KDB[1]), .Kbd_Available(KDB[2]), .RAM_In_0(I0),
    .Kbd_ASCII_Data(KDB_DATA), .RAM_In_1(I1), .TTY_Enable(TTY_EN), .RAM_In_2(I2), .RAM_In_3(I3),
    .TTY_ASCII_Data(TTY_DATA), .Reset(RST), .RAM_Out_0(ram_1_data_out_0), .Clock(CLK),
    .RAM_Out_1(ram_1_data_out_1), .Stop(halt), .RAM_Out_2(ram_1_data_out_2), .RAM_Out_3(ram_1_data_out_3),
    .Mask(Mask), .Read_Time(ram_1_read_time), .Write_Time(ram_1_write_time), .nRead_Write(R_W),
    .Chip_Select(CS));
  D_Flip_Flop d_ff_2 (.clk(CLK), .D(d_ff_1_q), .Qn(LCLR), .reset(Reset_out));  // open: Q, preset, en
  or or_1 (RST, LCLR, LoadRAM);
  Clock clock_1 (.out(CLK));
  Multiplexer #(.width(32), .enable("false")) multiplexer_1 (.in0(I0), .in1(LData), .out(RI0), .sel(LoadRAM));
  Multiplexer #(.width(32), .enable("false")) multiplexer_2 (.in0(I1), .in1(LData), .out(RI1), .sel(LoadRAM));
  Multiplexer #(.width(32), .enable("false")) multiplexer_3 (.in0(I2), .in1(LData), .out(RI2), .sel(LoadRAM));
  Multiplexer #(.width(32), .enable("false")) multiplexer_4 (.in0(I3), .in1(LData), .out(RI3), .sel(LoadRAM));
  and and_1 (LoadRAM, ~DESHABILITAR_DISPATCHER, LoadRAMOn);  // AND_Gate
  Multiplexer #(.width(16), .enable("false")) multiplexer_5 (.in0(Addr), .in1(LAddr), .out(RAddr), .sel(LoadRAM));
  Multiplexer #(.width(4), .enable("false")) multiplexer_6 (.in0(Mask), .in1(LMask), .out(RMask), .sel(LoadRAM));
  Multiplexer #(.enable("false")) multiplexer_7 (.in0(CS), .in1(LW), .out(RCS), .sel(LoadRAM));
  Multiplexer #(.enable("false")) multiplexer_8 (.in0(R_W), .in1(LW), .out(R_R_W), .sel(LoadRAM));

  // Notes on the sheet:
  //   NO MODIFICAR
  //   Keyboard
endmodule

module RAM (
  input  [15:0] Address,
  input  [31:0] Data_In_0,
  input  [31:0] Data_In_1,
  input  [31:0] Data_In_2,
  input  [31:0] Data_In_3,
  input  [3:0] Mask,
  input  nRead_Write,
  input  Chip_Select,
  input  Reset,
  output [31:0] Data_Out_0,
  output [31:0] Data_Out_1,
  output [31:0] Data_Out_2,
  output [31:0] Data_Out_3,
  output [3:0] Read_Time,
  output [3:0] Write_Time
);

  wire and_2_out, and_3_out, and_4_out, and_5_out, and_6_out, and_7_out, and_8_out, and_9_out, Changed, CLK,
       comparator_2_eq, comparator_3_eq, comparator_4_eq, comparator_5_eq, comparator_6_eq, Count,
       demultiplexer_3_out0, Idle, Idle_q, Load, Load0, Load1, nand_1_out, or_1_out, or_2_out, or_3_out,
       or_4_out, or_5_out, or_6_out, or_7_out, or_8_out, or_9_out, or_10_out, Proc_q, Update_Mem, Zero_Time;
  wire [3:0] counter_1_q, multiplexer_1_out, subtractor_1_out;
  wire [31:0] register_1_q, register_2_q, register_3_q, register_4_q, register_5_q;

  // Probe on 4'b0011
  // Probe on 4'b0010
  Multiplexer #(.width(4), .enable("false")) multiplexer_1 (
    .in0(4'b0011), .in1(4'b0010), .out(multiplexer_1_out), .sel(nRead_Write));
  or or_1 (or_1_out, Idle, Update_Mem);
  or or_2 (or_2_out, ~Chip_Select, Reset);  // OR_Gate
  Subtractor #(.width(4)) subtractor_1 (.a(multiplexer_1_out), .b(4'b0010), .out(subtractor_1_out));  // open: bin, bout
  D_Flip_Flop u_Idle (.clk(CLK), .D(or_1_out), .Q(Idle_q), .preset(or_2_out));  // open: Qn, en, reset
  Demultiplexer #(.enable("false")) demultiplexer_1 (.out0(Idle), .out1(Load0), .in(Idle_q), .sel(Changed));
  // Probe on counter_1_q
  Counter #(.width(4), .max('hf)) counter_1 (
    .load(Load), .D(subtractor_1_out), .count(Count), .Q(counter_1_q), .clk(CLK), .clr(or_3_out));  // open: carry
  or or_3 (or_3_out, ~Chip_Select, Reset);  // OR_Gate
  Comparator_part #(.width(4), .mode("unsigned")) comparator_1 (
    .a(4'b0000), .b(counter_1_q), .eq(Zero_Time));  // open: gt, lt
  or or_4 (or_4_out, Count, Load0, Load1);
  Register #(.width(32)) register_1 (.D(Data_In_0), .en(Chip_Select), .Q(register_1_q), .clk(CLK), .clr(or_5_out));
  or or_5 (or_5_out, ~Chip_Select, Reset);  // OR_Gate
  Register #(.width(32)) register_2 (.D(Data_In_1), .en(Chip_Select), .Q(register_2_q), .clk(CLK), .clr(or_6_out));
  or or_6 (or_6_out, ~Chip_Select, Reset);  // OR_Gate
  Register #(.width(32)) register_3 (.D(Data_In_2), .en(Chip_Select), .Q(register_3_q), .clk(CLK), .clr(or_7_out));
  or or_7 (or_7_out, ~Chip_Select, Reset);  // OR_Gate
  Register #(.width(32)) register_4 (.D(Data_In_3), .en(Chip_Select), .Q(register_4_q), .clk(CLK), .clr(or_8_out));
  or or_8 (or_8_out, ~Chip_Select, Reset);  // OR_Gate
  Register #(.width(32)) register_5 (
    .D({{11{1'b1}}, nRead_Write, Mask, Address}), .en(Chip_Select), .Q(register_5_q), .clk(CLK),
    .clr(or_9_out));
  or or_9 (or_9_out, ~Chip_Select, Reset);  // OR_Gate
  D_Flip_Flop Proc (.clk(CLK), .D(or_4_out), .Q(Proc_q), .reset(or_10_out));  // open: Qn, preset, en
  or or_10 (or_10_out, ~Chip_Select, Reset);  // OR_Gate
  Demultiplexer #(.enable("false")) demultiplexer_2 (
    .out0(Count), .out1(Update_Mem), .in(demultiplexer_3_out0), .sel(Zero_Time));
  Demultiplexer #(.enable("false")) demultiplexer_3 (
    .out0(demultiplexer_3_out0), .out1(Load1), .in(Proc_q), .sel(Changed));
  Clock clock_1 (.out(CLK));
  Comparator_part #(.width(32)) comparator_2 (.a(register_1_q), .b(Data_In_0), .eq(comparator_2_eq));  // open: gt, lt
  Comparator_part #(.width(32)) comparator_3 (.a(register_2_q), .b(Data_In_1), .eq(comparator_3_eq));  // open: gt, lt
  Comparator_part #(.width(32)) comparator_4 (.a(register_3_q), .b(Data_In_2), .eq(comparator_4_eq));  // open: gt, lt
  Comparator_part #(.width(32)) comparator_5 (.a(register_4_q), .b(Data_In_3), .eq(comparator_5_eq));  // open: gt, lt
  Comparator_part #(.width(32)) comparator_6 (
    .a(register_5_q), .b({{11{1'b1}}, nRead_Write, Mask, Address}), .eq(comparator_6_eq));  // open: gt, lt
  nand nand_1 (nand_1_out, comparator_6_eq, comparator_2_eq, comparator_3_eq, comparator_4_eq, comparator_5_eq);
  and and_1 (Changed, nand_1_out, Chip_Select);
  or or_11 (Load, Count, Load1, Load0);
  and and_2 (and_2_out, Mask[0], Update_Mem, nRead_Write);
  and and_3 (and_3_out, Mask[1], Update_Mem, nRead_Write);
  and and_4 (and_4_out, Mask[2], Update_Mem, nRead_Write);
  and and_5 (and_5_out, Mask[3], Update_Mem, nRead_Write);
  RAM_part #(.addrWidth(16), .dataWidth(32), .bus("separate")) ram_1 (
    .addr(Address), .din(Data_In_0), .data(Data_Out_0), .str(and_2_out), .sel(Chip_Select), .clk(CLK),
    .ld(and_6_out), .clr(Reset));
  and and_6 (and_6_out, ~nRead_Write, Idle);  // AND_Gate
  RAM_part #(.addrWidth(16), .dataWidth(32), .bus("separate")) ram_2 (
    .addr(Address), .din(Data_In_1), .data(Data_Out_1), .str(and_3_out), .sel(Chip_Select), .clk(CLK),
    .ld(and_7_out), .clr(Reset));
  and and_7 (and_7_out, ~nRead_Write, Idle);  // AND_Gate
  RAM_part #(.addrWidth(16), .dataWidth(32), .bus("separate")) ram_3 (
    .addr(Address), .din(Data_In_2), .data(Data_Out_2), .str(and_4_out), .sel(Chip_Select), .clk(CLK),
    .ld(and_8_out), .clr(Reset));
  and and_8 (and_8_out, ~nRead_Write, Idle);  // AND_Gate
  RAM_part #(.addrWidth(16), .dataWidth(32), .bus("separate")) ram_4 (
    .addr(Address), .din(Data_In_3), .data(Data_Out_3), .str(and_5_out), .sel(Chip_Select), .clk(CLK),
    .ld(and_9_out), .clr(Reset));
  and and_9 (and_9_out, ~nRead_Write, Idle);  // AND_Gate

  assign Read_Time = 4'b0011;
  assign Write_Time = 4'b0010;

  // Other names for the same wires on the sheet: M0 = Mask[0]; M1 = Mask[1]; M2 = Mask[2]; M3 = Mask[3];
  //   RW = nRead_Write; CLR = Reset; CS = Chip_Select; Load2 = Count

  // Notes on the sheet:
  //   NO MODIFICAR
  //   excepto quizás los valores RT y WT
  //   BANK0
  //   BANK1
  //   BANK2
  //   BANK3
endmodule

module S_MIPS (
  input  Kbd_Available,
  input  [31:0] RAM_Out_0,
  input  [6:0] Kbd_ASCII_Data,
  input  [31:0] RAM_Out_1,
  input  [31:0] RAM_Out_2,
  input  Reset,
  input  Clock,
  input  [31:0] RAM_Out_3,
  input  [3:0] Read_Time,
  input  [3:0] Write_Time,
  output [15:0] Address,
  output Kbd_Enable,
  output Kbd_Clear,
  output TTY_Enable,
  output [6:0] TTY_ASCII_Data,
  output Stop,
  output [31:0] RAM_In_0,
  output [31:0] RAM_In_1,
  output [31:0] RAM_In_2,
  output [31:0] RAM_In_3,
  output [3:0] Mask,
  output nRead_Write,
  output Chip_Select
);

  wire d_ready, enable_kbd, Enable_PC, Get_Data, Get_Inst, i_ready, Next, or_1_out, or_2_out, or_3_out, R_W,
       R_W_1, Save_Instruction, start, TTY, w_ready, Write;
  wire [2:0] TYPE;
  wire [31:0] ADDR, DATA, Instruction;

  Control_Unit control_unit_1 (
    .in_2(Clock), .in_1(Reset), .in_6(start), .in_3(TTY), .in_7(d_ready), .out_11(R_W), .out_9(Enable_PC),
    .out_15(Stop), .out_10(Save_Instruction), .out_14(TTY_Enable), .out_13(enable_kbd), .out_12(Write),
    .in_4(TYPE), .in_5(w_ready), .out_16(Get_Data), .in_8(i_ready), .out_17(Get_Inst));
  RAM_HANDLER ram_handler_1 (
    .Read_Time(Read_Time), .ADDRESS(ADDR), .Write_Time(Write_Time), .RAM_Out_0(RAM_Out_0),
    .RAM_Out_2(RAM_Out_2), .RAM_Out_1(RAM_Out_1), .RAM_Out_3(RAM_Out_3), .Write_in_RAM(Write),
    .Get_Instruction(Get_Inst), .Get_Data(Get_Data), .Clk(Clock), .Rst(Reset), .out_13(Instruction),
    .Address_2(Address), .Mask(Mask), .Chip_Select(Chip_Select), .out_19(w_ready), .out_18(d_ready),
    .out_16(i_ready), .R_W(nRead_Write), .R_W_data_path(R_W_1));
  Litlle_Endian litlle_endian_1 (.INPUT(DATA), .OUTPUT(RAM_In_0));
  or or_1 (or_1_out, R_W, R_W_1);
  D_Flip_Flop #(.trigger("falling")) d_ff_1 (.clk(Clock), .D(Reset), .Q(start));  // open: Qn, preset, en, reset
  and and_1 (Kbd_Enable, Kbd_Available, enable_kbd);
  D_Flip_Flop #(.trigger("falling")) d_ff_2 (
    .clk(Clock), .D(Get_Inst), .Q(Next), .en(or_2_out));  // open: Qn, preset, reset
  or or_2 (or_2_out, Get_Inst, i_ready);
  DATA_PATH data_path_1 (
    .Instruction(Instruction), .ADDR(ADDR), .DATA(DATA), .Clk(Clock), .Rst(Reset), .R_W(or_1_out),
    .Enable_PC(Enable_PC), .TTY_DATA(TTY_ASCII_Data), .Save_Instruct(Save_Instruction),
    .KBD_ascii(Kbd_ASCII_Data), .Go_Next_Instruct(Next), .Kbd_available(Kbd_Available), .TTY(TTY),
    .Output(TYPE), .write(or_3_out));
  or or_3 (or_3_out, Write, Get_Data);

  assign Kbd_Clear = Clock;
  assign RAM_In_1 = RAM_In_0;
  assign RAM_In_2 = RAM_In_0;
  assign RAM_In_3 = RAM_In_0;

  // Other names for the same wires on the sheet: CLR = Reset; CS = Chip_Select; KBD_AVAIL = Kbd_Available;
  //   CLK = Clock; KBD_CLR = Clock; KBD_DATA[6:0] = Kbd_ASCII_Data; RAM_A[15:0] = Address;
  //   RAM_INPUT_0[31:0] = RAM_In_0; RAM_INPUT_1[31:0] = RAM_In_0; RAM_INPUT_2[31:0] = RAM_In_0;
  //   RAM_INPUT_3[31:0] = RAM_In_0; RAM_MASK[3:0] = Mask; RAM_OUTPUT_0[31:0] = RAM_Out_0;
  //   RAM_OUTPUT_1[31:0] = RAM_Out_1; RAM_OUTPUT_2[31:0] = RAM_Out_2; RAM_OUTPUT_3[31:0] = RAM_Out_3;
  //   RW = nRead_Write; TTY_DATA[6:0] = TTY_ASCII_Data

  // Notes on the sheet:
  //   RAM ADDRESS
  //   DATA FROM RAM
  //   DATA TO RAM
  //   DATA WRITE MASK
  //   RAM TIMING
  //   RAM CONTROL
  //   KEYBOARD
  //   TTY
  //   SEQUENCING
endmodule

module RAM_Dispatcher (
  input  [3:0] WriteTime,
  input  Clock,
  input  CLR,
  output [31:0] Data,
  output [15:0] Address,
  output [3:0] Mask,
  output Finished,
  output Write
);

  wire demultiplexer_2_out1, demultiplexer_3_out1, End, IDLE_q, IncAddr, Load, or_1_out, or_2_out, While_q,
       WriteEnd;
  wire [3:0] counter_1_q;
  wire [31:0] CurrentAddress_q;

  Counter #(.width(32), .max('hffffffff)) CurrentAddress (
    .count(IncAddr), .Q({CurrentAddress_q[31:18], Address, CurrentAddress_q[1:0]}), .clk(Clock), .clr(CLR));  // open: load, D, carry
  or or_1 (or_1_out, IncAddr, demultiplexer_3_out1, Finished);
  D_Flip_Flop IDLE (.clk(Clock), .D(or_1_out), .Q(IDLE_q), .preset(CLR));  // open: Qn, en, reset
  Demultiplexer #(.enable("false")) demultiplexer_1 (.out0(Load), .out1(Finished), .in(IDLE_q), .sel(End));
  D_Flip_Flop While (.clk(Clock), .D(or_2_out), .Q(While_q), .reset(CLR));  // open: Qn, preset, en
  or or_2 (or_2_out, Write, Load);
  RAM_part #(.addrWidth(18), .dataWidth(32)) ram_1 (
    .addr({Address, CurrentAddress_q[1:0]}), .data(Data), .clk(Clock));  // open: sel, ld, clr
  Demultiplexer #(.enable("false")) demultiplexer_2 (
    .out0(Write), .out1(demultiplexer_2_out1), .in(While_q), .sel(WriteEnd));
  Decoder #(.select(2)) decoder_1 (
    .out0(Mask[0]), .out1(Mask[1]), .out2(Mask[2]), .out3(Mask[3]), .sel(CurrentAddress_q[1:0]));  // open: en
  Demultiplexer #(.enable("false")) demultiplexer_3 (
    .out0(IncAddr), .out1(demultiplexer_3_out1), .in(demultiplexer_2_out1), .sel(End));
  Counter #(.width(4), .max('hf)) counter_1 (
    .load(Load), .D(WriteTime), .count(Write), .Q(counter_1_q), .clk(Clock));  // open: carry, clr
  Comparator_part #(.width(32)) comparator_1 (.a(Data), .b({32{1'b1}}), .eq(End));  // open: gt, lt
  Comparator_part #(.width(4)) comparator_2 (.a(4'b0000), .b(counter_1_q), .eq(WriteEnd));  // open: gt, lt

  // Other names for the same wires on the sheet: CLK = Clock; Count = Write; WT[3:0] = WriteTime
endmodule

module REGISTER_File (
  input  [4:0] DA,
  input  [31:0] DI,
  input  R_W,
  input  [4:0] SA,
  input  [4:0] SB,
  input  Clk,
  input  Push,
  input  Reset,
  input  SP,
  output [31:0] A,
  output [31:0] SP_2,
  output [31:0] B
);

  wire I1, I2, I3, I4, I5, I6, I7, I8, I9, I10, I11, I12, I13, I14, I15, I16, I17, I18, I19, I20, I21, I22,
       I23, I24, I25, I26, I27, I28, I29, I30, I31, I32, save_sp;
  wire [31:0] adder_1_out, DI_SP, multiplexer_1_out, O1, O2, O3, O4, O5, O6, O7, O8, O9, O10, O11, O12, O13,
       O14, O15, O16, O17, O18, O19, O20, O21, O22, O23, O24, O25, O26, O27, O28, O29, O30, O31,
       subtractor_1_out;

  Demultiplexer #(.select(5)) demultiplexer_1 (
    .out0(I1), .out1(I2), .out2(I3), .out3(I4), .out4(I5), .out5(I6), .out6(I7), .out7(I8), .out8(I9),
    .out9(I10), .out10(I11), .out11(I12), .out12(I13), .out13(I14), .out14(I15), .out15(I16), .out16(I17),
    .out17(I18), .out18(I19), .out19(I20), .out20(I21), .out21(I22), .out22(I23), .out23(I24), .out24(I25),
    .out25(I26), .out26(I27), .out27(I28), .out28(I29), .out29(I30), .out30(I31), .out31(I32), .in(R_W),
    .sel(DA));  // open: en
  Register #(.width(32), .trigger("falling")) register_1 (.D(DI), .en(I1), .Q(O1), .clk(Clk), .clr(Reset));
  Register #(.width(32), .trigger("falling")) register_2 (.D(DI), .en(I5), .Q(O5), .clk(Clk), .clr(Reset));
  Register #(.width(32), .trigger("falling")) register_3 (.D(DI), .en(I9), .Q(O9), .clk(Clk), .clr(Reset));
  Register #(.width(32), .trigger("falling")) register_4 (.D(DI), .en(I13), .Q(O13), .clk(Clk), .clr(Reset));
  Register #(.width(32), .trigger("falling")) register_5 (.D(DI), .en(I17), .Q(O17), .clk(Clk), .clr(Reset));
  Register #(.width(32), .trigger("falling")) register_6 (.D(DI), .en(I21), .Q(O21), .clk(Clk), .clr(Reset));
  Register #(.width(32), .trigger("falling")) register_7 (.D(DI), .en(I25), .Q(O25), .clk(Clk), .clr(Reset));
  Register #(.width(32), .trigger("falling")) register_8 (.D(DI), .en(I29), .Q(O29), .clk(Clk), .clr(Reset));
  Subtractor #(.width(32)) subtractor_1 (.a(SP_2), .b(32'h4), .out(subtractor_1_out));  // open: bin, bout
  Adder #(.width(32)) adder_1 (.a(SP_2), .b(32'h4), .out(adder_1_out));  // open: cin, cout
  Multiplexer #(.width(32), .enable("false")) multiplexer_1 (
    .in0(subtractor_1_out), .in1(adder_1_out), .out(multiplexer_1_out), .sel(Push));
  Register #(.width(32), .trigger("falling")) register_9 (.D(DI), .en(I2), .Q(O2), .clk(Clk), .clr(Reset));
  Register #(.width(32), .trigger("falling")) register_10 (.D(DI), .en(I6), .Q(O6), .clk(Clk), .clr(Reset));
  Register #(.width(32), .trigger("falling")) register_11 (.D(DI), .en(I10), .Q(O10), .clk(Clk), .clr(Reset));
  Register #(.width(32), .trigger("falling")) register_12 (.D(DI), .en(I14), .Q(O14), .clk(Clk), .clr(Reset));
  Register #(.width(32), .trigger("falling")) register_13 (.D(DI), .en(I18), .Q(O18), .clk(Clk), .clr(Reset));
  Register #(.width(32), .trigger("falling")) register_14 (.D(DI), .en(I22), .Q(O22), .clk(Clk), .clr(Reset));
  Register #(.width(32), .trigger("falling")) register_15 (.D(DI), .en(I26), .Q(O26), .clk(Clk), .clr(Reset));
  Register #(.width(32), .trigger("falling")) register_16 (.D(DI), .en(I30), .Q(O30), .clk(Clk), .clr(Reset));
  Multiplexer #(.width(32), .enable("false")) multiplexer_2 (.in0(DI), .in1(multiplexer_1_out), .out(DI_SP), .sel(SP));
  Register #(.width(32), .trigger("falling")) register_17 (.D(DI), .en(I3), .Q(O3), .clk(Clk), .clr(Reset));
  Register #(.width(32), .trigger("falling")) register_18 (.D(DI), .en(I7), .Q(O7), .clk(Clk), .clr(Reset));
  Register #(.width(32), .trigger("falling")) register_19 (.D(DI), .en(I11), .Q(O11), .clk(Clk), .clr(Reset));
  Register #(.width(32), .trigger("falling")) register_20 (.D(DI), .en(I15), .Q(O15), .clk(Clk), .clr(Reset));
  Register #(.width(32), .trigger("falling")) register_21 (.D(DI), .en(I19), .Q(O19), .clk(Clk), .clr(Reset));
  Register #(.width(32), .trigger("falling")) register_22 (.D(DI), .en(I23), .Q(O23), .clk(Clk), .clr(Reset));
  Register #(.width(32), .trigger("falling")) register_23 (.D(DI), .en(I27), .Q(O27), .clk(Clk), .clr(Reset));
  Register #(.width(32), .trigger("falling")) register_24 (.D(DI), .en(I31), .Q(O31), .clk(Clk), .clr(Reset));
  or or_1 (save_sp, I32, SP);
  Register #(.width(32), .trigger("falling")) register_25 (.D(DI), .en(I4), .Q(O4), .clk(Clk), .clr(Reset));
  Register #(.width(32), .trigger("falling")) register_26 (.D(DI), .en(I8), .Q(O8), .clk(Clk), .clr(Reset));
  Register #(.width(32), .trigger("falling")) register_27 (.D(DI), .en(I12), .Q(O12), .clk(Clk), .clr(Reset));
  Register #(.width(32), .trigger("falling")) register_28 (.D(DI), .en(I16), .Q(O16), .clk(Clk), .clr(Reset));
  Register #(.width(32), .trigger("falling")) register_29 (.D(DI), .en(I20), .Q(O20), .clk(Clk), .clr(Reset));
  Register #(.width(32), .trigger("falling")) register_30 (.D(DI), .en(I24), .Q(O24), .clk(Clk), .clr(Reset));
  Register #(.width(32), .trigger("falling")) register_31 (.D(DI), .en(I28), .Q(O28), .clk(Clk), .clr(Reset));
  Register #(.width(32), .trigger("falling")) register_32 (.D(DI_SP), .en(save_sp), .Q(SP_2), .clk(Clk), .clr(Reset));
  Multiplexer #(.select(5), .width(32), .enable("false")) multiplexer_3 (
    .in0(O1), .in1(O2), .in2(O3), .in3(O4), .in4(O5), .in5(O6), .in6(O7), .in7(O8), .in8(O9), .in9(O10),
    .in10(O11), .in11(O12), .in12(O13), .in13(O14), .in14(O15), .in15(O16), .in16(O17), .in17(O18),
    .in18(O19), .in19(O20), .in20(O21), .in21(O22), .in22(O23), .in23(O24), .in24(O25), .in25(O26),
    .in26(O27), .in27(O28), .in28(O29), .in29(O30), .in30(O31), .in31(SP_2), .out(A), .sel(SA));
  Multiplexer #(.select(5), .width(32), .enable("false")) multiplexer_4 (
    .in0(O1), .in1(O2), .in2(O3), .in3(O4), .in4(O5), .in5(O6), .in6(O7), .in7(O8), .in8(O9), .in9(O10),
    .in10(O11), .in11(O12), .in12(O13), .in13(O14), .in14(O15), .in15(O16), .in16(O17), .in17(O18),
    .in18(O19), .in19(O20), .in20(O21), .in21(O22), .in22(O23), .in23(O24), .in24(O25), .in25(O26),
    .in26(O27), .in27(O28), .in28(O29), .in29(O30), .in30(O31), .in31(SP_2), .out(B), .sel(SB));

  // Other names for the same wires on the sheet: O32[31:0] = SP_2; OUT_A[31:0] = A; OUT_B[31:0] = B; pop = Push

  // Notes on the sheet:
  //   Inputs
  //   Data Address
  //   Data In
  //   Read/Write
  //   Selector A
  //   Selector B
  //   Registers
  //   Data A
  //   Data B
  //   Outputs
endmodule

module ALU (
  input  rst,
  input  enable,
  input  in_3,
  input  [31:0] Input,
  input  [31:0] Input_2,
  input  [3:0] in_6,
  output [31:0] Output,
  output [31:0] Output_2,
  output [31:0] Output_3
);

  wire sign_A, sign_B, tunnel;
  wire [31:0] addition, \and , bgtz, equal, high, low, multiplexer_2_out, multiplexer_3_out, \nand , \nor ,
       not_equal, \or , remainder, result, slt, sltu, subtraction, \xor ;

  assign \and  = Input & Input_2;  // AND_Gate and_1, 32 bits wide
  assign \or  = Input | Input_2;  // OR_Gate or_1, 32 bits wide
  assign \nand  = ~(Input & Input_2);  // NAND_Gate nand_1, 32 bits wide
  assign \nor  = ~(Input | Input_2);  // NOR_Gate nor_1, 32 bits wide
  assign \xor  = Input ^ Input_2;  // XOR_Gate xor_1, 32 bits wide
  Adder #(.width(32)) adder_1 (.a(Input), .b(Input_2), .out(addition));  // open: cin, cout
  Subtractor #(.width(32)) subtractor_1 (.a(Input), .b(Input_2), .out(subtraction));  // open: bin, bout
  Sign sign_1 (.in_1(Input), .Sign(sign_A));
  Sign sign_2 (.in_1(Input_2), .Sign(sign_B));
  Multiplier multiplier_1 (.in_1(Input), .in_2(sign_A), .in_4(Input_2), .Output(high), .Output_2(low), .in_3(sign_B));
  Divider divider_1 (.in_1(Input), .in_4(Input_2), .out_5(result), .out_6(remainder), .in_3(sign_B), .in_2(sign_A));
  Comparator comparator_1 (
    .in_1(Input), .in_2(Input_2), .less_than(slt), .less_than_unsigned(sltu), .greater_than(bgtz),
    .equal(equal), .not_equal(not_equal));
  Multiplexer #(.select(4), .width(32), .enable("false")) multiplexer_1 (
    .in0(addition), .in1(subtraction), .in2(slt), .in3(sltu), .in4(\xor ), .in5(\or ), .in6(\and ),
    .in7(\nor ), .in12(bgtz), .in13(equal), .in14(not_equal), .out(Output), .sel(in_6));  // open: in8, in9, in10, in11, in15
  and and_2 (tunnel, in_6[1], ~in_6[2], in_6[3]);  // AND_Gate
  Multiplexer #(.width(32), .enable("false")) multiplexer_2 (
    .in0(low), .in1(result), .out(multiplexer_2_out), .sel(tunnel));
  Multiplexer #(.width(32), .enable("false")) multiplexer_3 (
    .in0(high), .in1(remainder), .out(multiplexer_3_out), .sel(tunnel));
  Register #(.width(32)) register_1 (.D(multiplexer_2_out), .en(enable), .Q(Output_2), .clk(in_3), .clr(rst));
  Register #(.width(32)) register_2 (.D(multiplexer_3_out), .en(enable), .Q(Output_3), .clk(in_3), .clr(rst));

  // Other names for the same wires on the sheet: A[31:0] = Input; B[31:0] = Input_2; clock = in_3;
  //   high_t[31:0] = Output_3; low_t[31:0] = Output_2; _0 = in_6[0]; selector[3:0] = in_6; _1 = in_6[1]; _2 = in_6[2];
  //   _3 = in_6[3]

  // Notes on the sheet:
  //   ALU
endmodule

module Multiplier (
  input  [31:0] in_1,
  input  in_2,
  input  in_3,
  input  [31:0] in_4,
  output [31:0] Output,
  output [31:0] Output_2
);

  wire adder_1_cout, adder_3_cout, adder_5_cout, and_1_out, c1, c2, CA, CB;
  wire [31:0] A_2, A_CB, adder_1_out, adder_2_out, adder_3_out, adder_4_out, and_2_out, and_3_out, B_2, B_CA,
       bit_extender_2_out, bit_extender_3_out, C_AB, high, High_X, low, Low_X, multiplier_2_cout,
       multiplier_2_out, shift_left_3_out_3, shift_left_4_out_3, shift_left_5_out_3, shift_left_6_out_3;

  and and_1 (and_1_out, CA, CB);
  assign C_AB = {{31{1'b0}}, and_1_out};  // Bit_Extender bit_extender_1
  assign bit_extender_2_out = {{31{CB}}, CB};  // Bit_Extender bit_extender_2
  assign bit_extender_3_out = {{31{CA}}, CA};  // Bit_Extender bit_extender_3
  Multiplier_part #(.width(32)) multiplier_1 (.a(in_1), .b(in_4), .out(low), .cout(high));  // open: cin
  Shift_Right shift_right_1 (.input_a(in_1), .result(A_2), .bit_output(CA), .bit_input(1'b0));
  assign and_2_out = A_2 & bit_extender_2_out;  // AND_Gate and_2, 32 bits wide
  assign and_3_out = B_2 & bit_extender_3_out;  // AND_Gate and_3, 32 bits wide
  Shift_Right shift_right_2 (.input_a(in_4), .result(B_2), .bit_output(CB), .bit_input(1'b0));
  Shift_Left shift_left_1 (.in_2(and_2_out), .out_3(A_CB), .in_1(1'b0));  // open: Output
  Shift_Left shift_left_2 (.in_2(and_3_out), .out_3(B_CA), .in_1(1'b0));  // open: Output
  Multiplier_part #(.width(32)) multiplier_2 (
    .a(A_2), .b(B_2), .out(multiplier_2_out), .cout(multiplier_2_cout));  // open: cin
  Shift_Left shift_left_3 (.in_2(multiplier_2_out), .out_3(shift_left_3_out_3), .in_1(1'b0), .Output(c1));
  Shift_Left shift_left_4 (.in_2(multiplier_2_cout), .out_3(shift_left_4_out_3), .in_1(c1));  // open: Output
  Shift_Left shift_left_5 (.in_2(shift_left_3_out_3), .out_3(shift_left_5_out_3), .in_1(1'b0), .Output(c2));
  Shift_Left shift_left_6 (.in_2(shift_left_4_out_3), .out_3(shift_left_6_out_3), .in_1(c2));  // open: Output
  Multiplexer #(.width(32), .enable("false")) multiplexer_1 (.in0(High_X), .in1(high), .out(Output), .sel(in_2));
  Multiplexer #(.width(32), .enable("false")) multiplexer_2 (.in0(Low_X), .in1(low), .out(Output_2), .sel(in_3));
  Adder #(.width(32)) adder_1 (.a(shift_left_5_out_3), .b(A_CB), .out(adder_1_out), .cout(adder_1_cout));  // open: cin
  // Probe on High_X
  Adder #(.width(32)) adder_2 (
    .a(shift_left_6_out_3), .b({32{1'b0}}), .out(adder_2_out), .cin(adder_1_cout));  // open: cout
  Adder #(.width(32)) adder_3 (.a(adder_1_out), .b(B_CA), .out(adder_3_out), .cout(adder_3_cout));  // open: cin
  Adder #(.width(32)) adder_4 (.a(adder_2_out), .b({32{1'b0}}), .out(adder_4_out), .cin(adder_3_cout));  // open: cout
  Adder #(.width(32)) adder_5 (.a(adder_3_out), .b(C_AB), .out(Low_X), .cout(adder_5_cout));  // open: cin
  Adder #(.width(32)) adder_6 (.a(adder_4_out), .b({32{1'b0}}), .out(High_X), .cin(adder_5_cout));  // open: cout

  // Other names for the same wires on the sheet: A[31:0] = in_1; B[31:0] = in_4; sign_A = in_2; sign_B = in_3

  // Notes on the sheet:
  //   Multiplier
endmodule

module Divider (
  input  [31:0] in_1,
  input  in_2,
  input  in_3,
  input  [31:0] in_4,
  output [31:0] out_5,
  output [31:0] out_6
);

  wire division, minus_A, minus_B, xor_2_out;
  wire [31:0] A_t, adder_1_out, B_t, division_t_t, multiplexer_4_out, negator_1_out, negator_2_out,
       negator_3_out, negator_4_out, R, rest, subtractor_1_out;

  Negator #(.width(32)) negator_1 (.in(in_1), .out(negator_1_out));
  and and_1 (minus_A, in_1[31], in_2);
  and and_2 (minus_B, in_3, in_4[31]);
  Multiplexer #(.width(32), .enable("false")) multiplexer_1 (.in0(in_1), .in1(negator_1_out), .out(A_t), .sel(minus_A));
  Negator #(.width(32)) negator_2 (.in(in_4), .out(negator_2_out));
  xor xor_1 (division, minus_A, minus_B);
  Negator #(.width(32)) negator_3 (.in(division_t_t), .out(negator_3_out));
  Multiplexer #(.width(32), .enable("false")) multiplexer_2 (.in0(in_4), .in1(negator_2_out), .out(B_t), .sel(minus_B));
  Multiplexer #(.width(32), .enable("false")) multiplexer_3 (
    .in0(division_t_t), .in1(negator_3_out), .out(out_5), .sel(division));
  Divider_part #(.width(32)) divider_1 (.a(A_t), .b(B_t), .out(rest), .rem(R));  // open: upper
  Subtractor #(.width(32)) subtractor_1 (.a(B_t), .b(R), .out(subtractor_1_out));  // open: bin, bout
  Multiplexer #(.width(32), .enable("false")) multiplexer_4 (
    .in0(rest), .in1(adder_1_out), .out(multiplexer_4_out), .sel(minus_A));
  Adder #(.width(32)) adder_1 (.b(32'h1), .out(adder_1_out));  // open: a, cin, cout
  Multiplexer #(.width(32), .enable("false")) multiplexer_5 (
    .in0(R), .in1(subtractor_1_out), .out(out_6), .sel(minus_A));
  Negator #(.width(32)) negator_4 (.in(multiplexer_4_out), .out(negator_4_out));
  Multiplexer #(.width(32), .enable("false")) multiplexer_6 (
    .in0(multiplexer_4_out), .in1(negator_4_out), .out(out_5), .sel(xor_2_out));
  xor xor_2 (xor_2_out, minus_A, minus_B);

  // Other names for the same wires on the sheet: A[31:0] = in_1; B[31:0] = in_4; division_t[31:0] = out_5;
  //   remainder[31:0] = out_6; sign_A = in_2; sign_B = in_3

  // Notes on the sheet:
  //   Divider
endmodule

module Comparator (
  input  [31:0] in_1,
  input  [31:0] in_2,
  output [31:0] greater_than,
  output [31:0] equal,
  output [31:0] less_than,
  output [31:0] not_equal,
  output [31:0] less_than_unsigned
);

  wire and_1_out, bit_A, bit_B, comparator_1_eq, comparator_1_lt, comparator_2_gt, comparator_3_lt,
       comparator_4_eq, not_1_out, or_1_out, sign_A, sign_B;
  wire [31:0] shift_right_1_result, shift_right_2_result;

  Shift_Right shift_right_1 (.input_a(in_1), .result(shift_right_1_result), .bit_output(bit_A), .bit_input(1'b0));
  Shift_Right shift_right_2 (.input_a(in_2), .result(shift_right_2_result), .bit_output(bit_B), .bit_input(1'b0));
  Comparator_part #(.width(32)) comparator_1 (
    .a(shift_right_1_result), .b(shift_right_2_result), .eq(comparator_1_eq), .lt(comparator_1_lt));  // open: gt
  Comparator_part #(.width(32)) comparator_2 (.a(in_1), .b(in_2), .gt(comparator_2_gt));  // open: eq, lt
  Comparator_part #(.width(32)) comparator_3 (.a(in_1), .b(in_2), .lt(comparator_3_lt));  // open: gt, eq
  assign greater_than = {{31{1'b0}}, comparator_2_gt};  // Bit_Extender bit_extender_1
  assign less_than = {{31{1'b0}}, comparator_3_lt};  // Bit_Extender bit_extender_2
  and and_1 (and_1_out, ~bit_A, bit_B, comparator_1_eq);  // AND_Gate
  or or_1 (or_1_out, and_1_out, comparator_1_lt);
  assign less_than_unsigned = {{31{1'b0}}, or_1_out};  // Bit_Extender bit_extender_3
  assign equal = {{31{1'b0}}, comparator_4_eq};  // Bit_Extender bit_extender_4
  Comparator_part #(.width(32)) comparator_4 (.a(in_1), .b(in_2), .eq(comparator_4_eq));  // open: gt, lt
  assign not_equal = {{31{1'b0}}, not_1_out};  // Bit_Extender bit_extender_5
  not not_1 (not_1_out, comparator_4_eq);
  Sign sign_1 (.in_1(in_1), .Sign(sign_A));
  Sign sign_2 (.in_1(in_2), .Sign(sign_B));

  // Other names for the same wires on the sheet: A[31:0] = in_1; B[31:0] = in_2

  // Notes on the sheet:
  //   Comparator
endmodule

module Shift_Right (
  input  [31:0] input_a,
  input  bit_input,
  output bit_output,
  output [31:0] result
);


  assign bit_output = input_a[0];
  assign result = {bit_input, input_a[31:1]};

  // Other names for the same wires on the sheet: _2_A[31:0] = {bit_input, input_a[31:1]}; A[31:0] = input_a

  // Notes on the sheet:
  //   Shift Right
endmodule

module Shift_Left (
  input  in_1,
  input  [31:0] in_2,
  output [31:0] out_3,
  output Output
);


  assign out_3 = {in_2[30:0], in_1};
  assign Output = in_2[31];

  // Other names for the same wires on the sheet: _2_A[31:0] = {in_2[30:0], in_1}; A[31:0] = in_2

  // Notes on the sheet:
  //   Shift Left
endmodule

module Branch_Control (
  input  in_1,
  input  in_2,
  input  [2:0] in_3,
  input  in_4,
  input  [31:0] in_5,
  input  [31:0] in_6,
  input  [31:0] in_7,
  input  [31:0] in_8,
  input  [25:0] in_9,
  output [31:0] New_PC
);

  wire and_1_out, comparator_1_eq, comparator_1_gt, comparator_1_lt, comparator_2_eq, Flag_Condition,
       not_1_out, or_1_out;
  wire [1:0] Selector;
  wire [31:0] adder_1_out, adder_2_out, jump_size, shifter_1_out;

  Shifter #(.width(32)) shifter_1 (.in(in_7), .\dist (5'b00010), .out(shifter_1_out));
  Comparator_part #(.width(32)) comparator_1 (
    .a(in_6), .b({32{1'b0}}), .gt(comparator_1_gt), .eq(comparator_1_eq), .lt(comparator_1_lt));
  or or_1 (or_1_out, comparator_1_eq, comparator_1_lt);
  Comparator_part #(.width(32)) comparator_2 (.a(in_6), .b(in_8), .eq(comparator_2_eq));  // open: gt, lt
  Adder #(.width(32)) adder_1 (.a(in_5), .b(32'h4), .out(adder_1_out));  // open: cin, cout
  Adder #(.width(32)) adder_2 (.a(adder_1_out), .b(shifter_1_out), .out(adder_2_out));  // open: cin, cout
  not not_1 (not_1_out, comparator_2_eq);
  Priority_Encoder #(.select(2)) priority_encoder_1 (
    .in0(1'b1), .in1(in_2), .in2(in_1), .out(Selector));  // open: in3, gs, en_out, en_in
  Multiplexer #(.width(32), .enable("false")) multiplexer_1 (
    .in0(adder_1_out), .in1(adder_2_out), .out(jump_size), .sel(and_1_out));
  and and_1 (and_1_out, in_4, Flag_Condition);
  Multiplexer #(.select(3), .enable("false")) multiplexer_2 (
    .in0(comparator_1_gt), .in1(or_1_out), .in2(comparator_1_lt), .in3(not_1_out), .in4(comparator_2_eq),
    .out(Flag_Condition), .sel(in_3));  // open: in5, in6, in7
  Multiplexer #(.select(2), .width(32), .enable("false")) multiplexer_3 (
    .in0(jump_size), .in1({in_5[31:28], in_9, 2'b00}), .in2(in_6), .out(New_PC), .sel(Selector));  // open: in3

  // Other names for the same wires on the sheet: A[31:0] = in_6; B[31:0] = in_8; Destiny[31:2] = {in_5[31:28], in_9};
  //   Destiny_Jump[25:0] = in_9; Instruction_Adress[31:0] = in_5; Enable_FC = in_4; jmp = in_2; jr = in_1;
  //   K[31:0] = in_7; Select_FC[2:0] = in_3

  // Notes on the sheet:
  //   Branch Control
endmodule

module Program_Counter (
  input  [31:0] in_1,
  input  in_2,
  input  in_3,
  input  in_4,
  output [31:0] out_5
);

  Register #(.width(32)) register_1 (.D(in_1), .en(in_2), .Q(out_5), .clk(in_3), .clr(in_4));

  // Other names for the same wires on the sheet: Clk = in_3; Input[31:0] = in_1; Reset = in_4; Swap = in_2

  // Notes on the sheet:
  //   Output
endmodule

// BLTZ
module INSTRUCTION_DECODER (
  input  [31:0] in_1,
  output [5:0] Op_code,
  output [5:0] Func_code,
  output [2:0] DI_Select,
  output [4:0] DA,
  output [31:0] K_const,
  output [4:0] SA,
  output [4:0] SB,
  output [2:0] \type ,
  output jmp,
  output JR,
  output [1:0] memory_select,
  output pop,
  output [2:0] Select_FC,
  output sw,
  output [25:0] DESTINY,
  output [3:0] Operation_ALU,
  output IMMED,
  output tty,
  output Enable_FC,
  output SW_LW,
  output STACK,
  output mul_div
);

  wire add, addi, alu_add, alu_and, ALU_Enable, alu_or, alu_slt, alu_sltu, alu_xor, \and , andi, ARITM_1,
       ARITM_2, beq, bgtz, blez, bltz, bne, BRANCH, DI_Enable, div, divu, halt, kbd, LOGIC, LOGIC2, lw, mfhi,
       mflo, MOV, mult, mulu, NOP, nop_t, \nor , \or , or_4_out, or_8_out, or_9_out, or_13_out, or_14_out,
       or_15_out, or_16_out, or_17_out, ori, Other, push, R1, R2, R3, rnd, Select_Registro, slt, slti, sltiu,
       sltu, SPECIAL, sub, TIPO_I, \xor , xori;
  wire [1:0] DA_Option;

  or or_1 (alu_slt, slt, slti);
  and and_1 (LOGIC, R1, in_1[5], ~in_1[4], ~in_1[3], in_1[2]);  // AND_Gate
  Comparator_part #(.width(32)) comparator_1 (.a(in_1), .b({32{1'b0}}), .eq(NOP));  // open: gt, lt
  and and_2 (LOGIC2, R1, in_1[5], ~in_1[4], in_1[3], ~in_1[2]);  // AND_Gate
  and and_3 (halt, R3, in_1[5], in_1[4], in_1[3], in_1[2], in_1[1], in_1[0]);
  and and_4 (SPECIAL, R3, ~in_1[4], ~in_1[3], ~in_1[2]);  // AND_Gate
  Priority_Encoder #(.select(4)) priority_encoder_1 (
    .in0(alu_add), .in1(sub), .in2(alu_slt), .in3(alu_sltu), .in4(alu_xor), .in5(alu_or), .in6(alu_and),
    .in7(\nor ), .in8(mult), .in9(mulu), .in10(div), .in11(divu), .in12(bgtz), .in13(beq), .in14(bne),
    .out(Operation_ALU), .gs(ALU_Enable));  // open: in15, en_out, en_in
  or or_2 (alu_sltu, sltu, sltiu);
  or or_3 (alu_xor, \xor , xori);
  and and_5 (\and , LOGIC, ~in_1[1], ~in_1[0]);  // AND_Gate
  and and_6 (\or , LOGIC, ~in_1[1], in_1[0]);  // AND_Gate
  and and_7 (\xor , LOGIC2, ~in_1[1], ~in_1[0]);  // AND_Gate
  and and_8 (slt, LOGIC2, in_1[1], ~in_1[0]);  // AND_Gate
  and and_9 (tty, SPECIAL, ~in_1[1], in_1[0]);  // AND_Gate
  and and_10 (kbd, R3, ~in_1[5], ~in_1[4], ~in_1[3], in_1[2], ~in_1[1], ~in_1[0]);  // AND_Gate
  or or_4 (or_4_out, pop, lw);
  or or_5 (alu_or, \or , ori);
  or or_6 (alu_and, \and , andi);
  and and_11 (R1, ~in_1[31], ~in_1[30], ~in_1[29], ~in_1[28], ~in_1[27], ~in_1[26]);  // AND_Gate
  and and_12 (R2, in_1[31], in_1[30], in_1[29], ~in_1[28], ~in_1[27], ~in_1[26]);  // AND_Gate
  and and_13 (R3, in_1[31], in_1[30], in_1[29], in_1[28], in_1[27], in_1[26]);
  and and_14 (jmp, ~in_1[31], ~in_1[30], ~in_1[29], ~in_1[28], in_1[27], ~in_1[26]);  // AND_Gate
  and and_15 (rnd, SPECIAL, in_1[1], ~in_1[0]);  // AND_Gate
  Priority_Encoder priority_encoder_2 (
    .in0(ALU_Enable), .in1(mfhi), .in2(mflo), .in3(kbd), .in4(rnd), .in5(or_4_out), .out(DI_Select),
    .gs(DI_Enable));  // open: in6, in7, en_in, en_out
  and and_16 (\nor , LOGIC, in_1[1], in_1[0]);
  and and_17 (sltu, LOGIC2, in_1[1], in_1[0]);
  or or_7 (alu_add, lw, add, addi, sw);
  and and_18 (BRANCH, ~in_1[31], ~in_1[30], ~in_1[29]);  // AND_Gate
  and and_19 (ARITM_1, R1, in_1[5], ~in_1[4], ~in_1[3], ~in_1[2], ~in_1[0]);  // AND_Gate
  and and_20 (ARITM_2, R1, ~in_1[5], in_1[4], in_1[3], ~in_1[2]);  // AND_Gate
  or or_8 (or_8_out, lw, sw);
  or or_9 (or_9_out, push, pop);
  or or_10 (mul_div, mult, div, mulu, divu);
  and and_21 (bltz, BRANCH, ~in_1[28], ~in_1[27], in_1[26]);  // AND_Gate
  and and_22 (blez, BRANCH, in_1[28], in_1[27], ~in_1[26]);  // AND_Gate
  and and_23 (bgtz, BRANCH, in_1[28], in_1[27], in_1[26]);
  and and_24 (bne, BRANCH, in_1[28], ~in_1[27], in_1[26]);  // AND_Gate
  and and_25 (beq, BRANCH, in_1[28], ~in_1[27], ~in_1[26]);  // AND_Gate
  or or_11 (TIPO_I, BRANCH, IMMED, lw, sw);
  assign K_const = {{16{in_1[15]}}, in_1[15:0]};  // Bit_Extender bit_extender_1
  Priority_Encoder #(.select(2)) priority_encoder_3 (
    .in0(1'b1), .in1(or_8_out), .in2(or_9_out), .out(memory_select));  // open: in3, gs, en_out, en_in
  and and_26 (add, ARITM_1, ~in_1[1]);  // AND_Gate
  and and_27 (sub, ARITM_1, in_1[1]);
  and and_28 (mult, ARITM_2, ~in_1[1], ~in_1[0]);  // AND_Gate
  and and_29 (mulu, ARITM_2, ~in_1[1], in_1[0]);  // AND_Gate
  or or_12 (Enable_FC, bltz, blez, bgtz, bne, beq);
  Priority_Encoder priority_encoder_4 (
    .in0(bgtz), .in1(blez), .in2(bltz), .in3(bne), .in4(beq), .out(Select_FC));  // open: in5, in6, in7, en_in, gs, en_out
  and and_30 (slti, IMMED, ~in_1[28], in_1[27], ~in_1[26]);  // AND_Gate
  and and_31 (andi, IMMED, in_1[28], ~in_1[27], ~in_1[26]);  // AND_Gate
  and and_32 (addi, IMMED, ~in_1[28], ~in_1[27], ~in_1[26]);  // AND_Gate
  and and_33 (div, ARITM_2, in_1[1], ~in_1[0]);  // AND_Gate
  and and_34 (divu, ARITM_2, in_1[1], in_1[0]);
  and and_35 (IMMED, ~in_1[31], ~in_1[30], in_1[29]);  // AND_Gate
  and and_36 (sltiu, IMMED, ~in_1[28], in_1[27], in_1[26]);  // AND_Gate
  and and_37 (ori, IMMED, in_1[28], ~in_1[27], in_1[26]);  // AND_Gate
  and and_38 (xori, IMMED, in_1[28], in_1[27], ~in_1[26]);  // AND_Gate
  and and_39 (MOV, R1, ~in_1[5], in_1[4], ~in_1[3], ~in_1[2]);  // AND_Gate
  and and_40 (mfhi, MOV, ~in_1[1], ~in_1[0]);  // AND_Gate
  and and_41 (mflo, MOV, in_1[1], ~in_1[0]);  // AND_Gate
  or or_13 (or_13_out, R1, slt, R2, sltu, R3);
  Multiplexer #(.select(2), .width(5), .enable("false")) multiplexer_1 (
    .in0(in_1[20:16]), .in1(in_1[15:11]), .in2({5{1'b0}}), .in3({5{1'b1}}), .out(DA), .sel(DA_Option));
  Multiplexer #(.width(5), .enable("false")) multiplexer_2 (
    .in0(in_1[20:16]), .in1({5{1'b1}}), .out(SB), .sel(or_14_out));
  or or_14 (or_14_out, pop, push);
  Priority_Encoder #(.select(2)) priority_encoder_5 (
    .in0(1'b1), .in1(or_13_out), .in2(Enable_FC), .in3(push), .out(DA_Option));  // open: gs, en_out, en_in
  and and_42 (lw, in_1[31], ~in_1[30], ~in_1[29], ~in_1[28], in_1[27], in_1[26]);  // AND_Gate
  and and_43 (sw, in_1[31], ~in_1[30], in_1[29], ~in_1[28], in_1[27], in_1[26]);  // AND_Gate
  and and_44 (pop, R2, ~in_1[5], ~in_1[4], ~in_1[3], ~in_1[2], ~in_1[1], ~in_1[0]);  // AND_Gate
  and and_45 (push, R2, ~in_1[5], ~in_1[4], ~in_1[3], ~in_1[2], ~in_1[1], in_1[0]);  // AND_Gate
  and and_46 (Other, R1, ~in_1[5], ~in_1[4], ~in_1[2], ~in_1[1], ~in_1[0]);  // AND_Gate
  and and_47 (nop_t, Other, ~in_1[3]);  // AND_Gate
  and and_48 (JR, Other, in_1[3]);
  or or_15 (or_15_out, pop, lw);
  or or_16 (or_16_out, push, sw);
  or or_17 (or_17_out, jmp, NOP, JR, Enable_FC);
  or or_18 (Select_Registro, mfhi, kbd, ALU_Enable, rnd, mflo);
  or or_19 (SW_LW, lw, sw);
  or or_20 (STACK, pop, push);
  Priority_Encoder priority_encoder_6 (
    .in0(halt), .in1(Select_Registro), .in3(or_15_out), .in4(tty), .in6(or_16_out), .in7(or_17_out),
    .out(\type ));  // open: in2, in5, en_in, gs, en_out

  assign DESTINY = in_1[25:0];
  assign Func_code = in_1[5:0];
  assign Op_code = in_1[31:26];
  assign SA = in_1[25:21];

  // Other names for the same wires on the sheet: Branch_Jump = Enable_FC; CONSTANTE[31:0] = K_const;
  //   DI_Selector[2:0] = DI_Select; J_INSTRUCTION = jmp; A5 = in_1[0]; INSTRUCTION[31:0] = in_1;
  //   JUMP_DESTINY[25:0] = in_1[25:0]; A4 = in_1[1]; A3 = in_1[2]; A2 = in_1[3]; A1 = in_1[4]; A0 = in_1[5];
  //   X[4:0] = in_1[10:6]; RD[4:0] = in_1[15:11]; RT[4:0] = in_1[20:16]; RS[4:0] = in_1[25:21]; B5 = in_1[26];
  //   B4 = in_1[27]; B3 = in_1[28]; B2 = in_1[29]; B1 = in_1[30]; B0 = in_1[31]; Operation[3:0] = Operation_ALU

  // Notes on the sheet:
  //   INSTRUCTION
  //   INSTRUCTION SPLIT
  //   ALU Operations
  //   LOGIC INSTRUCTIONS
  //   SPECIAL INSTRUCTIONS
  //   Data Input Selector
  //   00 0000
  //   11 1000
  //   11 1111
  //   TIPO R
  //   00 0010
  //   TIPO R
  //   BRANCH INSTRUCTIONS
  //   Memory Address Selector
  //   ARITMETICAL INSTRUCTIONS
  //   TIPO I
  //   Branch Control Selector
  //   TIPO I
  //   TIPO R
  //   IMMEDIATE INSTRUCTIONS
  //   MOV INSTRUCTIONS
  //   TIPO R
  //   WORDS INSTRUCTIONS
  //   load words
  //   store words
  //   STACK INSTRUCTIONS
  //   TIPO I
  //   TIPO R
  //   OUTPUTS
endmodule

module Sign (
  input  [31:0] in_1,
  output Sign
);


  assign Sign = in_1[31];

  // Notes on the sheet:
  //   N
endmodule

module MEMORY_ADDRESS (
  input  [31:0] in_1,
  input  [31:0] in_2,
  input  in_3,
  input  in_4,
  input  [31:0] in_5,
  input  [1:0] in_6,
  output [31:0] OUT
);

  wire [31:0] multiplexer_2_out, New_SP, subtractor_1_out;

  Subtractor #(.width(32)) subtractor_1 (.a(in_1), .b(32'h4), .out(subtractor_1_out));  // open: bin, bout
  Multiplexer #(.width(32), .enable("false")) multiplexer_1 (
    .in0(in_1), .in1(subtractor_1_out), .out(New_SP), .sel(in_3));
  Multiplexer #(.select(2), .width(32), .enable("false")) multiplexer_2 (
    .in0(in_5), .in1(in_2), .in2(New_SP), .out(multiplexer_2_out), .sel(in_6));  // open: in3
  Multiplexer #(.width(32), .enable("false")) multiplexer_3 (
    .in0(multiplexer_2_out), .in1(in_5), .out(OUT), .sel(in_4));

  // Other names for the same wires on the sheet: ALU[31:0] = in_2; next = in_4; PC[31:0] = in_5; pop = in_3;
  //   select[1:0] = in_6; SP[31:0] = in_1
endmodule

module DATA_PATH (
  input  [31:0] Instruction,
  input  Clk,
  input  Rst,
  input  R_W,
  input  Enable_PC,
  input  Save_Instruct,
  input  [6:0] KBD_ascii,
  input  Go_Next_Instruct,
  input  Kbd_available,
  input  write,
  output [31:0] ADDR,
  output [31:0] DATA,
  output [6:0] TTY_DATA,
  output [2:0] Output,
  output TTY
);

  wire and_1_out, and_2_out, Enable_FC, IMMED, Jr, Jump, mul_div, not_1_out, or_1_out, pop, Select_Write,
       Stack, sw_lw;
  wire [1:0] Select_MA;
  wire [2:0] DI_Select, Select_FC;
  wire [3:0] Op_ALU;
  wire [4:0] DA_Select, SA, SB;
  wire [5:0] Funct_code, Op_code;
  wire [25:0] Jump_Destiny;
  wire [31:0] A, B, bit_extender_1_out, branch_control_1_new_pc, Data_IN, Hi, Instruction_t, K_constant, KBD,
       Lo, multiplexer_4_out, PC, random_1_out, Result, SP;
  wire [31:7] controlled_buffer_1_out;

  assign {controlled_buffer_1_out, TTY_DATA} = TTY ? A : 32'bz;  // Controlled_Buffer controlled_buffer_1
  Register #(.width(32)) register_1 (.D(Instruction), .en(Save_Instruct), .Q(Instruction_t), .clk(Clk));  // open: clr
  assign bit_extender_1_out = {{25{1'b0}}, KBD_ascii};  // Bit_Extender bit_extender_1
  Multiplexer #(.width(32), .enable("false")) multiplexer_1 (.in0(A), .in1(B), .out(DATA), .sel(Select_Write));
  Multiplexer #(.width(32), .enable("false")) multiplexer_2 (
    .in0({32{1'b1}}), .in1(bit_extender_1_out), .out(KBD), .sel(Kbd_available));
  Random #(.width(32)) random_1 (.clk(Clk), .out(random_1_out));  // open: next, clr
  INSTRUCTION_DECODER instruction_decoder_1 (
    .in_1(Instruction_t), .Op_code(Op_code), .DA(DA_Select), .Func_code(Funct_code), .K_const(K_constant),
    .SA(SA), .SB(SB), .DI_Select(DI_Select), .jmp(Jump), .memory_select(Select_MA), .pop(pop),
    .Select_FC(Select_FC), .JR(Jr), .DESTINY(Jump_Destiny), .Operation_ALU(Op_ALU), .\type (Output),
    .sw(Select_Write), .IMMED(IMMED), .tty(TTY), .Enable_FC(Enable_FC), .SW_LW(sw_lw), .STACK(Stack),
    .mul_div(mul_div));
  Multiplexer #(.select(3), .width(32), .enable("false")) multiplexer_3 (
    .in0(Result), .in1(Hi), .in2(Lo), .in3(KBD), .in4(random_1_out), .in5(Instruction), .out(Data_IN),
    .sel(DI_Select));  // open: in6, in7
  not not_1 (not_1_out, mul_div);
  and and_1 (and_1_out, write, Stack);
  REGISTER_File register_file_1 (
    .DA(DA_Select), .DI(Data_IN), .R_W(and_2_out), .SA(SA), .SB(SB), .Clk(Clk), .Reset(Rst), .A(A), .B(B),
    .SP_2(SP), .Push(pop), .SP(and_1_out));
  and and_2 (and_2_out, R_W, not_1_out);
  Multiplexer #(.width(32), .enable("false")) multiplexer_4 (
    .in0(B), .in1(K_constant), .out(multiplexer_4_out), .sel(or_1_out));
  or or_1 (or_1_out, IMMED, sw_lw);
  Branch_Control branch_control_1 (
    .in_5(PC), .in_2(Jump), .in_6(A), .in_8(B), .in_7(K_constant), .in_9(Jump_Destiny), .in_3(Select_FC),
    .in_1(Jr), .New_PC(branch_control_1_new_pc), .in_4(Enable_FC));
  ALU alu_1 (
    .in_3(Clk), .Input(A), .Input_2(multiplexer_4_out), .in_6(Op_ALU), .Output(Result), .Output_2(Lo),
    .Output_3(Hi), .enable(mul_div), .rst(Rst));
  MEMORY_ADDRESS memory_address_1 (
    .in_1(SP), .in_2(Result), .in_3(pop), .in_5(PC), .OUT(ADDR), .in_4(Go_Next_Instruct), .in_6(Select_MA));
  Program_Counter program_counter_1 (
    .in_1(branch_control_1_new_pc), .in_2(Enable_PC), .in_3(Clk), .out_5(PC), .in_4(Rst));

  // Other names for the same wires on the sheet: Data_t[31:0] = Instruction; Entry[31:0] = Instruction;
  //   KBD_data[6:0] = KBD_ascii; Put_in_Ram[31:0] = DATA; Type[2:0] = Output; write_get = write

  // Notes on the sheet:
  //   INPUTS
  //   Guardar Instruccion
  //   TTY
  //   Extender 32bits
  //   Write in Ram
  //   OUTPUTS
endmodule

module RAM_HANDLER (
  input  [3:0] Read_Time,
  input  [31:0] ADDRESS,
  input  [3:0] Write_Time,
  input  [31:0] RAM_Out_0,
  input  [31:0] RAM_Out_2,
  input  [31:0] RAM_Out_1,
  input  [31:0] RAM_Out_3,
  input  Write_in_RAM,
  input  Get_Instruction,
  input  Get_Data,
  input  Clk,
  input  Rst,
  output [31:0] out_13,
  output Chip_Select,
  output [15:0] Address_2,
  output out_16,
  output [3:0] Mask,
  output out_18,
  output out_19,
  output R_W,
  output R_W_data_path
);

  wire Its_reading, or_1_out, or_2_out, or_3_out, or_5_out, or_7_out, or_8_out, RD1, Read, RI1, RI2,
       time_cicle_1_its_ready, time_cicle_3_its_ready, W_stop;
  wire [1:0] Block;
  wire [31:0] OUTPUT_1, OUTPUT_2, OUTPUT_3, OUTPUT_4, register_1_q, register_2_q, register_3_q, register_4_q;

  Multiplexer #(.select(2), .width(32), .enable("false")) multiplexer_1 (
    .in0(OUTPUT_1), .in1(OUTPUT_2), .in2(OUTPUT_3), .in3(OUTPUT_4), .out(out_13), .sel(Block));
  Random random_1 ();  // open: clk, next, out, clr
  or or_1 (or_1_out, Get_Instruction, RI2);
  or or_2 (or_2_out, Write_in_RAM, W_stop);
  D_Flip_Flop #(.trigger("falling")) d_ff_1 (
    .clk(Clk), .D(Get_Instruction), .Q(RI1), .en(or_1_out));  // open: Qn, preset, reset
  D_Flip_Flop #(.trigger("falling")) d_ff_2 (
    .clk(Clk), .D(Get_Data), .Q(RD1), .en(or_3_out));  // open: Qn, preset, reset
  or or_3 (or_3_out, Get_Data, R_W_data_path);
  or or_4 (Its_reading, RI1, RI2, RD1, R_W_data_path);
  D_Flip_Flop #(.trigger("falling")) d_ff_3 (
    .clk(Clk), .D(Write_in_RAM), .Q(R_W), .en(or_2_out));  // open: Qn, preset, reset
  TIME_Cicle time_cicle_1 (
    .in_1(Clk), .in_2(or_7_out), .in_3(RI1), .in_4(Read_Time), .Its_ready(time_cicle_1_its_ready));
  TIME_Cicle time_cicle_2 (.in_1(Clk), .in_2(or_5_out), .in_3(R_W), .in_4(Write_Time), .Its_ready(W_stop));
  TIME_Cicle time_cicle_3 (
    .in_1(Clk), .in_2(or_8_out), .in_3(RD1), .in_4(Read_Time), .Its_ready(time_cicle_3_its_ready));
  Adress_Manager adress_manager_1 (.Adreess(ADDRESS), .Address(Address_2), .Bank(Mask), .out_3(Block));
  Register #(.width(32)) register_1 (.D(RAM_Out_0), .en(Read), .Q(register_1_q), .clk(Clk), .clr(Rst));
  Register #(.width(32)) register_2 (.D(RAM_Out_1), .en(Read), .Q(register_2_q), .clk(Clk), .clr(Rst));
  Register #(.width(32)) register_3 (.D(RAM_Out_2), .en(Read), .Q(register_3_q), .clk(Clk), .clr(Rst));
  Register #(.width(32)) register_4 (.D(RAM_Out_3), .en(Read), .Q(register_4_q), .clk(Clk), .clr(Rst));
  or or_5 (or_5_out, out_19, Rst);
  D_Flip_Flop #(.trigger("falling")) d_ff_4 (
    .clk(Clk), .D(time_cicle_1_its_ready), .Q(RI2), .reset(or_7_out));  // open: Qn, preset, en
  D_Flip_Flop #(.trigger("falling")) d_ff_5 (
    .clk(Clk), .D(time_cicle_3_its_ready), .Q(R_W_data_path), .reset(or_8_out));  // open: Qn, preset, en
  Litlle_Endian litlle_endian_1 (.INPUT(register_1_q), .OUTPUT(OUTPUT_1));
  Litlle_Endian litlle_endian_2 (.INPUT(register_2_q), .OUTPUT(OUTPUT_2));
  Litlle_Endian litlle_endian_3 (.INPUT(register_3_q), .OUTPUT(OUTPUT_3));
  Litlle_Endian litlle_endian_4 (.INPUT(register_4_q), .OUTPUT(OUTPUT_4));
  or or_6 (Read, RI1, RD1);
  D_Flip_Flop #(.trigger("falling")) d_ff_6 (.clk(Clk), .D(W_stop), .Q(out_19));  // open: Qn, preset, en, reset
  D_Flip_Flop #(.trigger("falling")) d_ff_7 (.clk(Clk), .D(RI2), .Q(out_16));  // open: Qn, preset, en, reset
  or or_7 (or_7_out, out_16, Rst);
  or or_8 (or_8_out, out_18, Rst);
  D_Flip_Flop #(.trigger("falling")) d_ff_8 (.clk(Clk), .D(R_W_data_path), .Q(out_18));  // open: Qn, preset, en, reset
  or or_9 (Chip_Select, Its_reading, R_W);

  // Other names for the same wires on the sheet: Block_Addr[15:0] = Address_2; CS = Chip_Select; Get_D = Get_Data;
  //   Get_I = Get_Instruction; Its_writing = R_W; OUTPUT[31:0] = out_13; RAM_OUTPUT_0[31:0] = RAM_Out_0;
  //   RAM_OUTPUT_1[31:0] = RAM_Out_1; RAM_OUTPUT_2[31:0] = RAM_Out_2; RAM_OUTPUT_3[31:0] = RAM_Out_3;
  //   RD2 = R_W_data_path; read_data_done = out_18; read_instruction_done = out_16; write = Write_in_RAM;
  //   write_done = out_19

  // Notes on the sheet:
  //   ADDREES
  //   INPUTS
  //   RAM DATA
  //   OUTPUTS
  //   RAM TIMING
  //   Do Write
  //   Do Read
  //   GET DATA PLACE
  //   SAVE DATA
endmodule

module Litlle_Endian (
  input  [31:0] INPUT,
  output [31:0] OUTPUT
);


  assign OUTPUT = {INPUT[7:0], INPUT[15:8], INPUT[23:16], INPUT[31:24]};

  // Notes on the sheet:
  //   LITTLE ENDIAN
endmodule

module TIME_Cicle (
  input  in_1,
  input  in_2,
  input  in_3,
  input  [3:0] in_4,
  output Its_ready
);

  wire [3:0] counter_1_q;

  Counter #(.width(4), .max('hf), .ongoal("continue")) counter_1 (
    .count(in_3), .Q(counter_1_q), .clk(in_1), .clr(in_2));  // open: load, D, carry
  Comparator_part #(.width(4)) comparator_1 (.a(in_4), .b(counter_1_q), .eq(Its_ready));  // open: gt, lt

  // Other names for the same wires on the sheet: Clk = in_1; Done = Its_ready; Rst = in_2; Start = in_3;
  //   Time_to_wait[3:0] = in_4

  // Notes on the sheet:
  //   INPUTS
  //   OTPUT
endmodule

module Adress_Manager (
  input  [31:0] Adreess,
  output [15:0] Address,
  output [1:0] out_3,
  output [3:0] Bank
);

  wire [3:0] divider_1_rem;
  wire [3:2] divider_2_out;
  wire [27:0] divider_1_rem_2;
  wire [31:16] divider_1_out;

  Divider_part #(.width(32)) divider_1 (
    .a(Adreess), .b(32'h10), .out({divider_1_out, Address}), .rem({divider_1_rem_2, divider_1_rem}));  // open: upper
  Divider_part #(.width(4)) divider_2 (
    .a(divider_1_rem), .b(4'b0100), .out({divider_2_out, out_3}));  // open: upper, rem
  Comparator_part #(.width(2)) comparator_1 (.a(out_3), .b(2'b00), .eq(Bank[0]));  // open: gt, lt
  Comparator_part #(.width(2)) comparator_2 (.a(out_3), .b(2'b01), .eq(Bank[1]));  // open: gt, lt
  Comparator_part #(.width(2)) comparator_3 (.a(out_3), .b(2'b10), .eq(Bank[2]));  // open: gt, lt
  Comparator_part #(.width(2)) comparator_4 (.a(out_3), .b(2'b11), .eq(Bank[3]));  // open: gt, lt
  // also tied to GND on the sheet: {divider_1_rem_2[0], divider_1_rem_2[1], divider_1_rem_2[2], divider_1_rem_2[3], divider_1_rem_2[4], divider_1_rem_2[5], divider_1_rem_2[6], divider_1_rem_2[7], divider_1_rem_2[8], divider_1_rem_2[9], divider_1_rem_2[10], divider_1_rem_2[11], divider_1_rem_2[12], divider_1_rem_2[13], divider_1_rem_2[14], divider_1_rem_2[15], divider_1_rem_2[16], divider_1_rem_2[17], divider_1_rem_2[18], divider_1_rem_2[19], divider_1_rem_2[20], divider_1_rem_2[21], divider_1_rem_2[22], divider_1_rem_2[23], divider_1_rem_2[24], divider_1_rem_2[25], divider_1_rem_2[26], divider_1_rem_2[27], divider_2_out[2], divider_2_out[3], divider_1_out[16], divider_1_out[17], divider_1_out[18], divider_1_out[19], divider_1_out[20], divider_1_out[21], divider_1_out[22], divider_1_out[23], divider_1_out[24], divider_1_out[25], divider_1_out[26], divider_1_out[27], divider_1_out[28], divider_1_out[29], divider_1_out[30], divider_1_out[31]}

  // Other names for the same wires on the sheet: Block[1:0] = out_3; RAM_address[15:0] = Address;
  //   Address_t[31:0] = Adreess; Mask[3:0] = Bank

  // Notes on the sheet:
  //   INPUT
  //   OUTPUTS
endmodule

module Control_Unit (
  input  in_1,
  input  in_2,
  input  in_3,
  input  [2:0] in_4,
  input  in_5,
  input  in_6,
  input  in_7,
  input  in_8,
  output out_9,
  output out_10,
  output out_11,
  output out_12,
  output out_13,
  output out_14,
  output out_15,
  output out_16,
  output out_17
);

  wire d_ff_1_q, d_ff_2_q, d_ff_4_q, d_ff_5_q, d_ff_6_q, demultiplexer_1_out0, demultiplexer_2_out0,
       demultiplexer_2_out1, demultiplexer_2_out4, demultiplexer_2_out7, demultiplexer_3_out0,
       demultiplexer_3_out1, demultiplexer_4_out0, demultiplexer_4_out1, or_1_out, or_2_out, or_3_out,
       or_4_out, or_5_out;
  wire [2:0] multiplexer_1_out;

  or or_1 (or_1_out, in_6, out_9);
  D_Flip_Flop #(.trigger("falling")) IDDLE (
    .clk(in_2), .D(or_1_out), .Q(out_17), .reset(in_1));  // open: Qn, preset, en
  or or_2 (or_2_out, demultiplexer_1_out0, out_17);
  D_Flip_Flop #(.trigger("falling")) d_ff_1 (
    .clk(in_2), .D(or_2_out), .Q(d_ff_1_q), .reset(in_1));  // open: Qn, preset, en
  Demultiplexer #(.enable("false")) demultiplexer_1 (
    .out0(demultiplexer_1_out0), .out1(out_10), .in(d_ff_1_q), .sel(in_8));
  D_Flip_Flop #(.trigger("falling")) d_ff_2 (
    .clk(in_2), .D(out_10), .Q(d_ff_2_q), .reset(in_1));  // open: Qn, preset, en
  Demultiplexer #(.select(3), .enable("false")) demultiplexer_2 (
    .out0(demultiplexer_2_out0), .out1(demultiplexer_2_out1), .out3(out_16), .out4(demultiplexer_2_out4),
    .out6(out_12), .out7(demultiplexer_2_out7), .in(d_ff_2_q), .sel(multiplexer_1_out));  // open: out2, out5
  Multiplexer #(.width(3), .enable("false")) multiplexer_1 (
    .in0(3'b000), .in1(in_4), .out(multiplexer_1_out), .sel(d_ff_2_q));
  or or_3 (or_3_out, out_15, demultiplexer_2_out0);
  or or_4 (or_4_out, demultiplexer_3_out0, out_16);
  or or_5 (or_5_out, demultiplexer_4_out0, out_12);
  D_Flip_Flop #(.trigger("falling")) d_ff_3 (
    .clk(in_2), .D(or_3_out), .Q(out_15), .reset(in_1));  // open: Qn, preset, en
  D_Flip_Flop #(.trigger("falling")) d_ff_4 (
    .clk(in_2), .D(or_4_out), .Q(d_ff_4_q), .reset(in_1));  // open: Qn, preset, en
  D_Flip_Flop #(.trigger("falling")) d_ff_5 (
    .clk(in_2), .D(or_5_out), .Q(d_ff_5_q), .reset(in_1));  // open: Qn, preset, en
  Demultiplexer #(.enable("false")) demultiplexer_3 (
    .out0(demultiplexer_3_out0), .out1(demultiplexer_3_out1), .in(d_ff_4_q), .sel(in_7));
  Demultiplexer #(.enable("false")) demultiplexer_4 (
    .out0(demultiplexer_4_out0), .out1(demultiplexer_4_out1), .in(d_ff_5_q), .sel(in_5));
  or or_6 (out_11, demultiplexer_2_out1, demultiplexer_3_out1);
  D_Flip_Flop #(.trigger("falling")) d_ff_6 (
    .clk(in_2), .D(out_11), .Q(d_ff_6_q), .reset(in_1));  // open: Qn, preset, en
  or or_7 (out_13, d_ff_6_q, demultiplexer_2_out4);
  or or_8 (out_9, out_13, demultiplexer_4_out1, demultiplexer_2_out7);
  and and_1 (out_14, in_3, out_13);

  // Other names for the same wires on the sheet: clk = in_2; data_done = in_7; En_IR = out_10; En_PC = out_9;
  //   En_RF = out_11; En_tty = out_14; end = out_15; get_dta = out_16; get_inst = out_17; instruction_done = in_8;
  //   op_type[2:0] = in_4; reset = in_1; start = in_6; En_kbd = out_13; tty = out_13; tty_Instruction = in_3;
  //   write = out_12; write_done = in_5

  // Notes on the sheet:
  //   Inputs
  //   Outputs
endmodule
